# Fritzing sketch Devre (saved by Fritzing 0.9.3b)
breadboards: 1

parts:
  R2 = Resistor [tolerance=±5% resistance=10k package="1206 [SMD]"]
  GY-NEO6MV2 = SUP500F [package=sup500f]
  Parça1 = Arduino Nano (Rev3.0)
  LCD1 = LCD screen

nets:
  N1: R2.Pin_0, LCD1.V0
  N2: R2.Pin_1, Parça1.GND, LCD1.LED+
  N3: GY-NEO6MV2.TX-O, Parça1.5V, LCD1.LED-
  N4: GY-NEO6MV2.GND, Parça1.D8

notes:
  GND: Black
  VCC: Red
  RX: Yellow
  TX: Green
